# Fritzing sketch energy-consumption-monitor (saved by Fritzing 0.9.9b)

parts:
  J17 = female pin header, 2 pins [form="♀ (female)"]
  J18 = female pin header, 2 pins [form="♀ (female)"]
  J19 = female pin header, 2 pins [form="♀ (female)"]
  J20 = female pin header, 2 pins [form="♀ (female)"]
  J21 = female pin header, 2 pins [form="♀ (female)"]
  J22 = female pin header, 2 pins [form="♀ (female)"]
  GSM_SIM_GPSR_SMS_SIM900_SIM2 = SIM800L [package=THT]
  microSD2 = MicroSD Card Module
  ZS-042_RTC2 = ZS-042 RTC Module
  LCD2004-I2C2 = LCD2004-I2C
  Mod2 = zmpt101b
  Part4 = ACS712 Current Sensor 5A 20A 30A
  o2 = Module display OLED I2C 128x64 SSD1306 [package=THT]
  TP2 = TP4056 [chip_label=TP4056 package="DIP (Dual Inline) [THT]"]
  U3 = LIPO-110mAh [package=lipo-110]
  J23 = female pin header, 2 pins [form="♀ (female)"]
  J24 = female pin header, 2 pins [form="♀ (female)"]
  J25 = female pin header, 2 pins [form="♀ (female)"]
  J26 = female pin header, 2 pins [form="♀ (female)"]
  J29 = female pin header, 2 pins [form="♀ (female)"]
  J30 = female pin header, 2 pins [form="♀ (female)"]
  J31 = female pin header, 2 pins [form="♀ (female)"]
  J32 = female pin header, 2 pins [form="♀ (female)"]
  M2 = RioRand LM2596
  Part5 = Arduino Mega 2560 (Rev3)
  J33 = female pin header, 2 pins [form="♀ (female)"]
  J34 = female pin header, 2 pins [form="♀ (female)"]

nets:
  N1: J17.pin1, J19.pin1, Part4.VCC
  N2: J17.pin2, J19.pin2, Part4.GND
  N3: J18.pin1, Part4.2, Part4.OUT, Part5.A1
  N4: J18.pin2, Mod2.OUT, Part5.A0
  N5: J20.pin1, Mod2.GND, J29.pin1
  N6: J20.pin2, Mod2.VCC, J29.pin2
  N7: J21.pin1, J22.pin1, GSM_SIM_GPSR_SMS_SIM900_SIM2.GND#5, Part5.GND
  N8: J21.pin2, J22.pin2, Part5.5V
  N9: GSM_SIM_GPSR_SMS_SIM900_SIM2.5V, J30.pin2
  N10: GSM_SIM_GPSR_SMS_SIM900_SIM2.GND#1, J30.pin1
  N11: GSM_SIM_GPSR_SMS_SIM900_SIM2.SIM_TXD, Part5.D10_PWM
  N12: GSM_SIM_GPSR_SMS_SIM900_SIM2.SIM_RXD, Part5.D11_PWM
  N13: microSD2.GND, J23.pin2
  N14: microSD2.VCC, J23.pin1
  N15: microSD2.MISO, Part5.D48
  N16: microSD2.MOSI, Part5.D49
  N17: microSD2.SCK, Part5.D50
  N18: microSD2.CS, Part5.D51
  N19: ZS-042_RTC2.GND, J25.pin2
  N20: ZS-042_RTC2.VCC, J25.pin1
  N21: ZS-042_RTC2.SDA, Part5.SDA
  N22: ZS-042_RTC2.SCL, Part5.SCL
  N23: LCD2004-I2C2.GND, J24.pin1
  N24: LCD2004-I2C2.VCC, J24.pin2
  N25: LCD2004-I2C2.SDA, J26.pin1
  N26: LCD2004-I2C2.SCL, J26.pin2
  N27: o2.GND, J33.pin2
  N28: o2.VCC, J33.pin1
  N29: o2.SCL, J34.pin2
  N30: o2.SDA, J34.pin1
  N31: TP2.pin1, J31.pin1
  N32: TP2.pin2, J31.pin2
  N33: TP2.pin3, M2.Pin_1
  N34: TP2.pin4, U3.+
  N35: TP2.pin5, U3.-
  N36: TP2.pin6, M2.Pin_2
  N37: J32.pin1, M2.Pin_3
  N38: J32.pin2, M2.Pin_4

custom parts:
  LCD2004-I2C: A standard character display with 4x20 characters. Comes in many colors with LCM2004 IIC attached.
  zmpt101b: Single phase ac active output voltate transformer module.
  ACS712 Current Sensor 5A 20A 30A: Remix by Michael Kubina http://www.kubina.info Original by: https://forum.fritzing.org/t/current-sensor-5a-acs712/7694 https://forum.fritzing.org/u/ArtHome ArtHome12@gmail.com
  Module display OLED I2C 128x64 SSD1306: Ecran OLED I2C SSD163 de 128x64 avec connexion I2C
  TP4056: A DIP stand-in part for whatever IC you want. With 6 pins on a 300mil dual inline package (DIP) footprint.
